// Logisim project adder.circ as structural Verilog: 3 circuits, main circuit main
module main (
  input  [15:0] B,
  input  [15:0] A,
  input  sub,
  output ovf,
  output [15:0] result
);

  wire fa_1_cout, fa_2_cout, fa_3_cout, fa_4_cout, fa_5_cout, fa_6_cout, fa_7_cout, fa_8_cout, fa_9_cout,
       fa_10_cout, fa_11_cout, fa_12_cout, fa_13_cout, fa_14_cout, fa_15_cout, fa_16_cout, xor_1_out,
       xor_2_out, xor_3_out, xor_4_out, xor_5_out, xor_6_out, xor_7_out, xor_8_out, xor_9_out, xor_10_out,
       xor_11_out, xor_12_out, xor_13_out, xor_14_out, xor_15_out, xor_16_out;

  xor xor_1 (xor_1_out, B[15], sub);
  FA fa_1 (.a(A[15]), .b(xor_1_out), .Cin(sub), .Cout(fa_1_cout), .Sum(result[15]));
  xor xor_2 (xor_2_out, B[13], sub);
  xor xor_3 (xor_3_out, B[14], sub);
  FA fa_2 (.a(A[13]), .b(xor_2_out), .Cin(fa_3_cout), .Cout(fa_2_cout), .Sum(result[13]));
  FA fa_3 (.a(A[14]), .b(xor_3_out), .Cin(fa_1_cout), .Cout(fa_3_cout), .Sum(result[14]));
  xor xor_4 (xor_4_out, B[12], sub);
  FA fa_4 (.a(A[12]), .b(xor_4_out), .Cin(fa_2_cout), .Cout(fa_4_cout), .Sum(result[12]));
  xor xor_5 (xor_5_out, B[11], sub);
  FA fa_5 (.a(A[11]), .b(xor_5_out), .Cin(fa_4_cout), .Cout(fa_5_cout), .Sum(result[11]));
  xor xor_6 (xor_6_out, B[10], sub);
  FA fa_6 (.a(A[9]), .b(xor_7_out), .Cin(fa_7_cout), .Cout(fa_6_cout), .Sum(result[9]));
  FA fa_7 (.a(A[10]), .b(xor_6_out), .Cin(fa_5_cout), .Cout(fa_7_cout), .Sum(result[10]));
  xor xor_7 (xor_7_out, B[9], sub);
  xor xor_8 (xor_8_out, B[8], sub);
  FA fa_8 (.a(A[8]), .b(xor_8_out), .Cin(fa_6_cout), .Cout(fa_8_cout), .Sum(result[8]));
  xor xor_9 (xor_9_out, B[7], sub);
  FA fa_9 (.a(A[7]), .b(xor_9_out), .Cin(fa_8_cout), .Cout(fa_9_cout), .Sum(result[7]));
  xor xor_10 (xor_10_out, B[6], sub);
  FA fa_10 (.a(A[5]), .b(xor_12_out), .Cin(fa_11_cout), .Cout(fa_10_cout), .Sum(result[5]));
  FA fa_11 (.a(A[6]), .b(xor_10_out), .Cin(fa_9_cout), .Cout(fa_11_cout), .Sum(result[6]));
  xor xor_11 (xor_11_out, B[4], sub);
  xor xor_12 (xor_12_out, B[5], sub);
  FA fa_12 (.a(A[4]), .b(xor_11_out), .Cin(fa_10_cout), .Cout(fa_12_cout), .Sum(result[4]));
  xor xor_13 (xor_13_out, B[3], sub);
  FA fa_13 (.a(A[3]), .b(xor_13_out), .Cin(fa_12_cout), .Cout(fa_13_cout), .Sum(result[3]));
  xor xor_14 (xor_14_out, B[2], sub);
  FA fa_14 (.a(A[2]), .b(xor_14_out), .Cin(fa_13_cout), .Cout(fa_14_cout), .Sum(result[2]));
  xor xor_15 (xor_15_out, B[0], sub);
  xor xor_16 (xor_16_out, B[1], sub);
  FA fa_15 (.a(A[0]), .b(xor_15_out), .Cin(fa_16_cout), .Cout(fa_15_cout), .Sum(result[0]));
  FA fa_16 (.a(A[1]), .b(xor_16_out), .Cin(fa_14_cout), .Cout(fa_16_cout), .Sum(result[1]));
  xor xor_17 (ovf, fa_16_cout, fa_15_cout);
endmodule

module FA (
  input  Cin,
  input  a,
  input  b,
  output Sum,
  output Cout
);

  wire and_1_out, and_2_out, xor_1_out;

  and and_1 (and_1_out, b, a);
  xor xor_1 (xor_1_out, a, b);
  or or_1 (Cout, and_1_out, and_2_out);
  and and_2 (and_2_out, xor_1_out, Cin);
  xor xor_2 (Sum, Cin, xor_1_out);
endmodule

module FA1 (
  input  [3:0] Sum,
  input  Cin,
  input  [3:0] A,
  input  [3:0] B,
  output Cout
);

  wire fa_1_cout, fa_2_cout, fa_3_cout;

  FA fa_1 (.a(A[0]), .b(B[0]), .Cin(Cin), .Cout(fa_1_cout), .Sum(Sum[0]));
  FA fa_2 (.a(A[1]), .b(B[1]), .Cin(fa_1_cout), .Cout(fa_2_cout), .Sum(Sum[1]));
  FA fa_3 (.a(A[2]), .b(B[2]), .Cin(fa_2_cout), .Cout(fa_3_cout), .Sum(Sum[2]));
  FA fa_4 (.a(A[3]), .b(B[3]), .Cin(fa_3_cout), .Cout(Cout), .Sum(Sum[3]));
endmodule
