// Logisim project adder2.circ as structural Verilog: 3 circuits, main circuit main
module main (
  input  [15:0] A,
  input  [15:0] B,
  input  Cin,
  input  sub,
  input  [15:0] result,
  input  ovf
);

  FA1 fa1_1 (.A(A[3:0]));  // open: Sum, B, Cin, Cout
  FA1 fa1_2 ();  // open: Sum, A, B, Cin, Cout
  FA1 fa1_3 ();  // open: Sum, A, B, Cin, Cout
endmodule

module FA (
  input  Cin,
  input  a,
  input  b,
  output Sum,
  output Cout
);

  wire and_1_out, and_2_out, xor_1_out;

  and and_1 (and_1_out, b, a);
  xor xor_1 (xor_1_out, a, b);
  or or_1 (Cout, and_1_out, and_2_out);
  and and_2 (and_2_out, xor_1_out, Cin);
  xor xor_2 (Sum, Cin, xor_1_out);
endmodule

module FA1 (
  input  Cin,
  input  [3:0] A,
  input  [3:0] B,
  output [3:0] Sum,
  output Cout
);

  wire fa_1_cout, fa_2_cout, fa_3_cout;

  FA fa_1 (.a(A[0]), .b(B[0]), .Cin(Cin), .Cout(fa_1_cout), .Sum(Sum[0]));
  FA fa_2 (.a(A[1]), .b(B[1]), .Cin(fa_1_cout), .Cout(fa_2_cout), .Sum(Sum[1]));
  FA fa_3 (.a(A[2]), .b(B[2]), .Cin(fa_2_cout), .Cout(fa_3_cout), .Sum(Sum[2]));
  FA fa_4 (.a(A[3]), .b(B[3]), .Cin(fa_3_cout), .Cout(Cout), .Sum(Sum[3]));
endmodule
