// Logisim project adder3.circ as structural Verilog: 3 circuits, main circuit main
module main (
  input  [15:0] A,
  input  [15:0] B,
  input  sub,
  input  Cin,
  input  [15:0] result,
  input  ovf,
  output Cout
);

  wire fa1_1_cout, fa1_2_cout, fa1_3_cout;
  wire [3:0] bit_extender_1_out, bit_extender_2_out, bit_extender_3_out, bit_extender_4_out, xor_1_out,
       xor_2_out, xor_3_out, xor_4_out;

  assign bit_extender_1_out = {{3{Cin}}, Cin};  // Bit_Extender bit_extender_1
  assign xor_1_out = bit_extender_1_out ^ A[3:0];  // XOR_Gate xor_1, 4 bits wide
  assign bit_extender_2_out = {{3{Cin}}, Cin};  // Bit_Extender bit_extender_2
  assign xor_2_out = bit_extender_2_out ^ A[7:4];  // XOR_Gate xor_2, 4 bits wide
  FA1 fa1_1 (.Sum(result[3:0]), .Cin(Cin), .A(xor_1_out), .B(B[3:0]), .Cout(fa1_1_cout));
  assign bit_extender_3_out = {{3{Cin}}, Cin};  // Bit_Extender bit_extender_3
  assign xor_3_out = bit_extender_3_out ^ A[11:8];  // XOR_Gate xor_3, 4 bits wide
  FA1 fa1_2 (.Sum(result[7:4]), .Cin(fa1_1_cout), .A(xor_2_out), .B(B[7:4]), .Cout(fa1_2_cout));
  assign bit_extender_4_out = {{3{Cin}}, Cin};  // Bit_Extender bit_extender_4
  assign xor_4_out = bit_extender_4_out ^ A[15:12];  // XOR_Gate xor_4, 4 bits wide
  FA1 fa1_3 (.Sum(result[11:8]), .Cin(fa1_2_cout), .A(xor_3_out), .B(B[11:8]), .Cout(fa1_3_cout));
  FA1 fa1_4 (.Sum(result[15:12]), .Cin(fa1_3_cout), .A(xor_4_out), .B(B[15:12]), .Cout(Cout));

  assign sub = Cin;
endmodule

module FA (
  input  Cin,
  input  a,
  input  b,
  output Sum,
  output Cout
);

  wire and_1_out, and_2_out, xor_1_out;

  and and_1 (and_1_out, b, a);
  xor xor_1 (xor_1_out, a, b);
  or or_1 (Cout, and_1_out, and_2_out);
  and and_2 (and_2_out, xor_1_out, Cin);
  xor xor_2 (Sum, Cin, xor_1_out);
endmodule

module FA1 (
  input  [3:0] Sum,
  input  Cin,
  input  [3:0] A,
  input  [3:0] B,
  output Cout
);

  wire fa_1_cout, fa_2_cout, fa_3_cout;

  FA fa_1 (.a(A[0]), .b(B[0]), .Cin(Cin), .Cout(fa_1_cout), .Sum(Sum[0]));
  FA fa_2 (.a(A[1]), .b(B[1]), .Cin(fa_1_cout), .Cout(fa_2_cout), .Sum(Sum[1]));
  FA fa_3 (.a(A[2]), .b(B[2]), .Cin(fa_2_cout), .Cout(fa_3_cout), .Sum(Sum[2]));
  FA fa_4 (.a(A[3]), .b(B[3]), .Cin(fa_3_cout), .Cout(Cout), .Sum(Sum[3]));
endmodule
