// Logisim project circuit1c.circ as structural Verilog: 1 circuit, main circuit main
module main (
  input  A,
  input  B,
  input  C,
  output out2,
  output out1
);

  wire and_1_out, and_2_out, and_3_out, and_4_out, and_5_out, and_6_out, not_1_out, not_2_out, not_3_out;

  not not_1 (not_1_out, B);
  not not_2 (not_2_out, A);
  not not_3 (not_3_out, C);
  and and_1 (and_1_out, not_2_out, not_1_out, C);
  and and_2 (and_2_out, not_2_out, B, not_3_out);
  and and_3 (and_3_out, B, C);
  and and_4 (and_4_out, A, not_3_out);
  and and_5 (and_5_out, A, B);
  and and_6 (and_6_out, not_2_out, not_1_out, not_3_out);
  or or_1 (out2, and_5_out, and_6_out);
  or or_2 (out1, and_1_out, and_2_out, and_3_out, and_4_out);
endmodule
