// Logisim project fsm.circ as structural Verilog: 1 circuit, main circuit main
module main (
  input  in1,
  input  in2,
  output out
);

  wire and_1_out, and_2_out, and_3_out, and_4_out, and_5_out, and_6_out, and_7_out, and_8_out, and_9_out,
       and_10_out, and_11_out, and_12_out, and_13_out, and_14_out, and_15_out, and_16_out, and_17_out,
       and_18_out, and_19_out, and_20_out, and_21_out, and_22_out, Clock, notIn1, notIn2, notQ0, notQ1,
       notQ2, or_1_out, or_2_out, or_3_out, or_4_out, or_5_out, or_6_out, or_7_out, or_8_out, or_9_out,
       or_10_out, Q0, Q1, Q2;

  and and_1 (and_1_out, notIn2, notIn1);
  and and_2 (and_2_out, in2, in1);
  and and_3 (and_3_out, notQ2, Q1, Q0);
  and and_4 (and_4_out, Q2, notQ1, notQ0);
  or or_1 (or_1_out, and_1_out, and_2_out);
  and and_5 (and_5_out, notQ1, notQ0);
  and and_6 (and_6_out, notQ2, Q1, Q0);
  and and_7 (and_7_out, notIn1, in2);
  and and_8 (and_8_out, in1, notIn2);
  and and_9 (and_9_out, notQ2, Q1, Q0);
  and and_10 (and_10_out, Q2, notQ0);
  and and_11 (and_11_out, notIn1, in2);
  and and_12 (and_12_out, in1, notIn2);
  and and_13 (and_13_out, notQ2, Q1, notQ0);
  and and_14 (and_14_out, Q2, Q1, Q0);
  and and_15 (and_15_out, notIn1, notIn2);
  and and_16 (and_16_out, in1, in2);
  and and_17 (and_17_out, notQ2, notQ1, notQ0, or_1_out);
  or or_2 (or_2_out, and_5_out, and_6_out);
  or or_3 (or_3_out, and_7_out, and_8_out);
  or or_4 (or_4_out, and_9_out, and_10_out);
  or or_5 (or_5_out, and_11_out, and_12_out);
  or or_6 (or_6_out, and_13_out, and_14_out);
  or or_7 (or_7_out, and_15_out, and_16_out);
  or or_8 (or_8_out, and_17_out, and_3_out, and_4_out);
  and and_18 (and_18_out, or_2_out, or_3_out);
  and and_19 (and_19_out, notQ2, Q1, notQ0);
  and and_20 (and_20_out, Q2, Q1, Q0);
  and and_21 (and_21_out, or_4_out, or_5_out);
  and and_22 (and_22_out, or_6_out, or_7_out);
  or or_9 (or_9_out, and_18_out, and_19_out, and_20_out);
  or or_10 (or_10_out, and_21_out, and_22_out);
  D_Flip_Flop FF2 (.D(or_8_out), .clk(Clock), .Q(Q2), .Qn(notQ2));  // open: preset, reset
  D_Flip_Flop FF1 (.D(or_9_out), .clk(Clock), .Q(Q1), .Qn(notQ1));  // open: preset, reset
  D_Flip_Flop FF0 (.D(or_10_out), .clk(Clock), .Q(Q0), .Qn(notQ0));  // open: preset, reset
  not not_1 (notIn1, in1);
  not not_2 (notIn2, in2);
  Clock clk (.out(Clock));
  and and_23 (out, Q1, Q0);

  // Other names for the same wires on the sheet: input1 = in1; input2 = in2
endmodule
