// Logisim project hw4.circ as structural Verilog: 12 circuits, main circuit main
module main (
  input  reset
);

  wire ALUinB, ALUop_ifpositive, ALUop_ifzero, br1, br2, clk, DMwe, if_beq, if_bgt, if_input, if_output,
       if_valid, JAL, JP, JR, memory_latch_1_oe_latched, memory_latch_1_we_latched, Nclk, or_1_out, Rdst,
       Rwd, RWE;
  wire [2:0] multiplexer_2_out, multiplexer_3_out, optype;
  wire [3:0] opcode;
  wire [6:0] data_write, keyboard_1_data;
  wire [11:0] Address, PC;
  wire [15:0] extended_immediate, full_adder_2_result, lw_address, lw_output, memory_latch_1_address_latched,
       memory_latch_1_data_in_latched, multiplexer_1_out, multiplexer_4_out, multiplexer_5_out,
       multiplexer_6_out, multiplexer_7_out, multiplexer_8_out, nextPC, PCplus1, Rd_value, rt_address;
  wire [15:7] Rs_value;
  wire [15:12] jump_address;

  Clock u_clk (.out(clk));
  full_adder full_adder_1 (.B({jump_address, PC}), .A(16'h1), .result(PCplus1));  // open: ovf, sub
  ROM #(.addrWidth(16), .dataWidth(16)) rom_1 (.addr({jump_address, PC}), .data({opcode, Address}));
  \reg  u_PC (.data_out({jump_address, PC}), .data_in(nextPC), .clk(clk), .write_enable(1'b1), .reset(reset));
  not not_1 (Nclk, clk);
  decoder decoder_1 (
    .opcode(opcode), .optype(optype), .Rdst(Rdst), .ALUinB(ALUinB), .RWE(RWE), .DMwe(DMwe), .Rwd(Rwd),
    .br1(br1), .br2(br2), .JP(JP), .JAL(JAL), .JR(JR), .if_input(if_input), .if_output(if_output));
  Multiplexer #(.width(16), .enable("false")) multiplexer_1 (
    .in0(multiplexer_7_out), .in1(Rd_value), .out(multiplexer_1_out), .sel(if_input));
  memory_latch memory_latch_1 (
    .address(lw_address), .WE(DMwe), .clk(clk), .data_in(rt_address),
    .address_latched(memory_latch_1_address_latched), .WE_latched(memory_latch_1_we_latched),
    .OE_latched(memory_latch_1_oe_latched), .data_in_latched(memory_latch_1_data_in_latched));
  RegisterFile registerfile_1 (
    .data_in(multiplexer_1_out), .rd(multiplexer_2_out), .clk(Nclk), .write_enable(RWE), .reset(reset),
    .rs1(Address[11:9]), .rs2(Address[8:6]), .rs1_content({Rs_value, data_write}), .rs2_content(rt_address));
  RAM #(.addrWidth(16), .dataWidth(16), .trigger("high"), .databus("bibus")) ram_1 (
    .addr(memory_latch_1_address_latched), .we(memory_latch_1_we_latched), .oe(memory_latch_1_oe_latched),
    .din(memory_latch_1_data_in_latched), .dout(lw_output));
  Multiplexer #(.width(3), .enable("false")) multiplexer_2 (
    .in0(multiplexer_3_out), .in1(3'b111), .out(multiplexer_2_out), .sel(JAL));
  Multiplexer #(.width(3), .enable("false")) multiplexer_3 (
    .in0(Address[8:6]), .in1(Address[5:3]), .out(multiplexer_3_out), .sel(Rdst));
  assign extended_immediate = {{10{Address[5]}}, Address[5:0]};  // Bit_Extender bit_extender_1
  Multiplexer #(.width(16), .enable("false")) multiplexer_4 (
    .in0(rt_address), .in1(extended_immediate), .out(multiplexer_4_out), .sel(ALUinB));
  full_adder full_adder_2 (.B(PCplus1), .A(extended_immediate), .result(full_adder_2_result));  // open: ovf, sub
  calc ALUop (
    .A({Rs_value, data_write}), .B(multiplexer_4_out), .optype(optype), .data_out(lw_address),
    .shamt(Address[2:0]), .ifZero(ALUop_ifzero), .ifPositive(ALUop_ifpositive));
  and and_1 (if_bgt, br2, ALUop_ifpositive);
  TTY #(.rows(13), .cols(80), .trigger("falling")) tty_1 (.data(data_write), .clk(clk), .we(if_output), .clr(reset));
  or or_1 (or_1_out, if_bgt, if_beq);
  and and_2 (if_beq, br1, ALUop_ifzero);
  Multiplexer #(.width(16), .enable("false")) multiplexer_5 (
    .in0(PCplus1), .in1(full_adder_2_result), .out(multiplexer_5_out), .sel(or_1_out));
  Multiplexer #(.width(16), .enable("false")) multiplexer_6 (
    .in0(lw_address), .in1(lw_output), .out(multiplexer_6_out), .sel(Rwd));
  Multiplexer #(.width(16), .enable("false")) multiplexer_7 (
    .in0(multiplexer_6_out), .in1(PCplus1), .out(multiplexer_7_out), .sel(JAL));
  Keyboard keyboard_1 (.clk(clk), .re(if_input), .clr(reset), .avail(if_valid), .data(keyboard_1_data));
  Multiplexer #(.width(16), .enable("false")) multiplexer_8 (
    .in0(multiplexer_5_out), .in1({jump_address, Address}), .out(multiplexer_8_out), .sel(JP));
  Multiplexer #(.width(16), .enable("false")) multiplexer_9 (
    .in0(multiplexer_8_out), .in1({Rs_value, data_write}), .out(nextPC), .sel(JR));
  data_reader data_reader_1 (.orginal_data(keyboard_1_data), .if_valid(if_valid), .data_read(Rd_value));

  // Other names for the same wires on the sheet: Rs_value[6:0] = data_write; immed[5:0] = Address[5:0];
  //   jump_address[11:0] = Address; Shamt[2:0] = Address[2:0]; Rd[2:0] = Address[5:3]; Rt[2:0] = Address[8:6];
  //   Rs[2:0] = Address[11:9]; PC[15:12] = jump_address
endmodule

module \reg  (
  input  [15:0] data_in,
  input  clk,
  input  write_enable,
  input  reset,
  output [15:0] data_out
);

  wire update;

  D_Flip_Flop d_ff_1 (.D(data_in[0]), .clk(update), .Q(data_out[0]), .reset(reset));  // open: Qn, preset
  D_Flip_Flop d_ff_2 (.D(data_in[1]), .clk(update), .Q(data_out[1]), .reset(reset));  // open: Qn, preset
  D_Flip_Flop d_ff_3 (.D(data_in[2]), .clk(update), .Q(data_out[2]), .reset(reset));  // open: Qn, preset
  D_Flip_Flop d_ff_4 (.D(data_in[3]), .clk(update), .Q(data_out[3]), .reset(reset));  // open: Qn, preset
  and and_1 (update, clk, write_enable);
  D_Flip_Flop d_ff_5 (.D(data_in[4]), .clk(update), .Q(data_out[4]), .reset(reset));  // open: Qn, preset
  D_Flip_Flop d_ff_6 (.D(data_in[5]), .clk(update), .Q(data_out[5]), .reset(reset));  // open: Qn, preset
  D_Flip_Flop d_ff_7 (.D(data_in[6]), .clk(update), .Q(data_out[6]), .reset(reset));  // open: Qn, preset
  D_Flip_Flop d_ff_8 (.D(data_in[7]), .clk(update), .Q(data_out[7]), .reset(reset));  // open: Qn, preset
  D_Flip_Flop d_ff_9 (.D(data_in[8]), .clk(update), .Q(data_out[8]), .reset(reset));  // open: Qn, preset
  D_Flip_Flop d_ff_10 (.D(data_in[9]), .clk(update), .Q(data_out[9]), .reset(reset));  // open: Qn, preset
  D_Flip_Flop d_ff_11 (.D(data_in[10]), .clk(update), .Q(data_out[10]), .reset(reset));  // open: Qn, preset
  D_Flip_Flop d_ff_12 (.D(data_in[11]), .clk(update), .Q(data_out[11]), .reset(reset));  // open: Qn, preset
  D_Flip_Flop d_ff_13 (.D(data_in[12]), .clk(update), .Q(data_out[12]), .reset(reset));  // open: Qn, preset
  D_Flip_Flop d_ff_14 (.D(data_in[13]), .clk(update), .Q(data_out[13]), .reset(reset));  // open: Qn, preset
  D_Flip_Flop d_ff_15 (.D(data_in[14]), .clk(update), .Q(data_out[14]), .reset(reset));  // open: Qn, preset
  D_Flip_Flop d_ff_16 (.D(data_in[15]), .clk(update), .Q(data_out[15]), .reset(reset));  // open: Qn, preset

  // Other names for the same wires on the sheet: in1 = data_in[0]; in2 = data_in[1]; in3 = data_in[2];
  //   in4 = data_in[3]; in5 = data_in[4]; in6 = data_in[5]; in7 = data_in[6]; in8 = data_in[7]; in9 = data_in[8];
  //   in10 = data_in[9]; in11 = data_in[10]; in12 = data_in[11]; in13 = data_in[12]; in14 = data_in[13];
  //   in15 = data_in[14]; in16 = data_in[15]; out1 = data_out[0]; out2 = data_out[1]; out3 = data_out[2];
  //   out4 = data_out[3]; out5 = data_out[4]; out6 = data_out[5]; out7 = data_out[6]; out8 = data_out[7];
  //   out9 = data_out[8]; out10 = data_out[9]; out11 = data_out[10]; out12 = data_out[11]; out13 = data_out[12];
  //   out14 = data_out[13]; out15 = data_out[14]; out16 = data_out[15]
endmodule

module RegisterFile (
  input  [15:0] data_in,
  input  [2:0] rd,
  input  clk,
  input  write_enable,
  input  reset,
  input  [2:0] rs1,
  input  [2:0] rs2,
  output [15:0] rs1_content,
  output [15:0] rs2_content
);

  wire in1, in2, in3, in4, in5, in6, in7, in8;
  wire [15:0] out2, out3, out4, out5, out6, out7, out8;

  Decoder #(.select(3)) decoder_1 (
    .out0(in1), .out1(in2), .out2(in3), .out3(in4), .out4(in5), .out5(in6), .out6(in7), .out7(in8), .sel(rd),
    .en(write_enable));
  // Probe on {16{1'b0}}
  // Probe on out2
  \reg  r1_2 (.data_out(out2), .data_in(data_in), .clk(clk), .write_enable(in2), .reset(reset));
  // Probe on out3
  \reg  r2_2 (.data_out(out3), .data_in(data_in), .clk(clk), .write_enable(in3), .reset(reset));
  // Probe on out4
  \reg  r3_2 (.data_out(out4), .data_in(data_in), .clk(clk), .write_enable(in4), .reset(reset));
  // Probe on out5
  \reg  r4_2 (.data_out(out5), .data_in(data_in), .clk(clk), .write_enable(in5), .reset(reset));
  // Probe on out6
  \reg  r5_2 (.data_out(out6), .data_in(data_in), .clk(clk), .write_enable(in6), .reset(reset));
  // Probe on out7
  \reg  r6_2 (.data_out(out7), .data_in(data_in), .clk(clk), .write_enable(in7), .reset(reset));
  // Probe on out8
  \reg  r7_2 (.data_out(out8), .data_in(data_in), .clk(clk), .write_enable(in8), .reset(reset));
  Multiplexer #(.select(3), .width(16), .enable("false")) multiplexer_1 (
    .in0({16{1'b0}}), .in1(out2), .in2(out3), .in3(out4), .in4(out5), .in5(out6), .in6(out7), .in7(out8),
    .out(rs1_content), .sel(rs1));
  Multiplexer #(.select(3), .width(16), .enable("false")) multiplexer_2 (
    .in0({16{1'b0}}), .in1(out2), .in2(out3), .in3(out4), .in4(out5), .in5(out6), .in6(out7), .in7(out8),
    .out(rs2_content), .sel(rs2));

  // Other names for the same wires on the sheet: data[15:0] = data_in; r = reset; w = write_enable
endmodule

module calc (
  input  [15:0] A,
  input  [15:0] B,
  input  [2:0] shamt,
  input  [2:0] optype,
  output [15:0] data_out,
  output ifZero,
  output ifPositive
);

  wire not_1_out, not_2_out;
  wire [15:0] add_result, and_1_out, difference, or_1_out, shl_1_rd, shra_1_rd, sub_result;

  subtrct diff (.B(B), .A(A), .data_out(difference));
  shra shra_1 (.rs(A), .rd(shra_1_rd), .shamt(shamt));
  shl shl_1 (.rs(A), .rd(shl_1_rd), .shamt(shamt));
  full_adder add (.B(A), .A(B), .result(add_result));  // open: ovf, sub
  full_adder sub (.B(B), .A(A), .result(sub_result), .sub(1'b1));  // open: ovf
  assign or_1_out = A | B;  // OR_Gate or_1, 16 bits wide
  assign and_1_out = A & B;  // AND_Gate and_1, 16 bits wide
  not not_1 (not_1_out, ifZero);
  not not_2 (not_2_out, difference[15]);
  nor nor_1 (ifZero, difference[0], difference[1], difference[2], difference[3], difference[4], difference[5], difference[6], difference[7], difference[8], difference[9], difference[10], difference[11], difference[12], difference[13], difference[14], difference[15]);
  and and_2 (ifPositive, not_1_out, not_2_out);
  Multiplexer #(.select(3), .width(16), .enable("false")) multiplexer_1 (
    .in0(add_result), .in1(sub_result), .in2(or_1_out), .in3(and_1_out), .in4(shra_1_rd), .in5(shl_1_rd),
    .out(data_out), .sel(optype));  // open: in6, in7

  // Other names for the same wires on the sheet: MSB = difference[15]
endmodule

module adder (
  input  Cin,
  input  a,
  input  b,
  output Sum,
  output Cout
);

  wire and_1_out, and_2_out, xor_1_out;

  and and_1 (and_1_out, b, a);
  xor xor_1 (xor_1_out, a, b);
  or or_1 (Cout, and_1_out, and_2_out);
  and and_2 (and_2_out, xor_1_out, Cin);
  xor xor_2 (Sum, Cin, xor_1_out);
endmodule

module full_adder (
  input  [15:0] B,
  input  [15:0] A,
  input  sub,
  output [15:0] result,
  output ovf
);

  wire adder_1_cout, adder_2_cout, adder_3_cout, adder_4_cout, adder_5_cout, adder_6_cout, adder_7_cout,
       adder_8_cout, adder_9_cout, adder_10_cout, adder_11_cout, adder_12_cout, adder_13_cout, adder_14_cout,
       adder_15_cout, adder_16_cout, xor_2_out, xor_3_out, xor_4_out, xor_5_out, xor_6_out, xor_7_out,
       xor_8_out, xor_9_out, xor_10_out, xor_11_out, xor_12_out, xor_13_out, xor_14_out, xor_15_out,
       xor_16_out, xor_17_out;

  xor xor_1 (ovf, adder_1_cout, adder_2_cout);
  adder adder_1 (.a(A[15]), .b(xor_2_out), .Sum(result[15]), .Cin(adder_2_cout), .Cout(adder_1_cout));
  xor xor_2 (xor_2_out, sub, B[15]);
  adder adder_2 (.a(A[14]), .b(xor_3_out), .Sum(result[14]), .Cin(adder_3_cout), .Cout(adder_2_cout));
  xor xor_3 (xor_3_out, sub, B[14]);
  adder adder_3 (.a(A[13]), .b(xor_4_out), .Sum(result[13]), .Cin(adder_4_cout), .Cout(adder_3_cout));
  xor xor_4 (xor_4_out, sub, B[13]);
  adder adder_4 (.a(A[12]), .b(xor_5_out), .Sum(result[12]), .Cin(adder_5_cout), .Cout(adder_4_cout));
  adder adder_5 (.a(A[11]), .b(xor_6_out), .Sum(result[11]), .Cin(adder_6_cout), .Cout(adder_5_cout));
  xor xor_5 (xor_5_out, sub, B[12]);
  adder adder_6 (.a(A[10]), .b(xor_7_out), .Sum(result[10]), .Cin(adder_7_cout), .Cout(adder_6_cout));
  xor xor_6 (xor_6_out, sub, B[11]);
  adder adder_7 (.a(A[9]), .b(xor_9_out), .Sum(result[9]), .Cin(adder_8_cout), .Cout(adder_7_cout));
  xor xor_7 (xor_7_out, sub, B[10]);
  adder adder_8 (.a(A[8]), .b(xor_8_out), .Sum(result[8]), .Cin(adder_9_cout), .Cout(adder_8_cout));
  xor xor_8 (xor_8_out, sub, B[8]);
  xor xor_9 (xor_9_out, sub, B[9]);
  adder adder_9 (.a(A[7]), .b(xor_10_out), .Sum(result[7]), .Cin(adder_10_cout), .Cout(adder_9_cout));
  xor xor_10 (xor_10_out, sub, B[7]);
  adder adder_10 (.a(A[6]), .b(xor_11_out), .Sum(result[6]), .Cin(adder_11_cout), .Cout(adder_10_cout));
  xor xor_11 (xor_11_out, sub, B[6]);
  adder adder_11 (.a(A[5]), .b(xor_12_out), .Sum(result[5]), .Cin(adder_12_cout), .Cout(adder_11_cout));
  adder adder_12 (.a(A[4]), .b(xor_13_out), .Sum(result[4]), .Cin(adder_13_cout), .Cout(adder_12_cout));
  xor xor_12 (xor_12_out, sub, B[5]);
  adder adder_13 (.a(A[3]), .b(xor_14_out), .Sum(result[3]), .Cin(adder_14_cout), .Cout(adder_13_cout));
  xor xor_13 (xor_13_out, sub, B[4]);
  adder adder_14 (.a(A[2]), .b(xor_16_out), .Sum(result[2]), .Cin(adder_15_cout), .Cout(adder_14_cout));
  xor xor_14 (xor_14_out, sub, B[3]);
  adder adder_15 (.a(A[1]), .b(xor_15_out), .Sum(result[1]), .Cin(adder_16_cout), .Cout(adder_15_cout));
  xor xor_15 (xor_15_out, sub, B[1]);
  xor xor_16 (xor_16_out, sub, B[2]);
  adder adder_16 (.a(A[0]), .b(xor_17_out), .Sum(result[0]), .Cin(sub), .Cout(adder_16_cout));
  xor xor_17 (xor_17_out, sub, B[0]);

  // Other names for the same wires on the sheet: b1 = A[0]; b2 = A[1]; b3 = A[2]; b4 = A[3]; b5 = A[4]; b6 = A[5];
  //   b7 = A[6]; b8 = A[7]; b9 = A[8]; b10 = A[9]; b11 = A[10]; b12 = A[11]; b13 = A[12]; b14 = A[13]; b15 = A[14];
  //   b16 = A[15]; a1 = B[0]; a2 = B[1]; a3 = B[2]; a4 = B[3]; a5 = B[4]; a6 = B[5]; a7 = B[6]; a8 = B[7]; a9 = B[8];
  //   a10 = B[9]; a11 = B[10]; a12 = B[11]; a13 = B[12]; a14 = B[13]; a15 = B[14]; a16 = B[15]
endmodule

module decoder (
  input  [3:0] opcode,
  output DMwe,
  output Rwd,
  output br1,
  output br2,
  output JP,
  output JAL,
  output JR,
  output if_input,
  output if_output,
  output Rdst,
  output ALUinB,
  output RWE,
  output [2:0] optype
);

  wire add, addi, \and , j, \or , or_4_out, shl, shra, sub;

  or or_1 (optype[2], shra, shl);
  or or_2 (optype[1], \or , \and );
  or or_3 (optype[0], shl, sub, \and , br2, br1);
  Decoder #(.select(4), .enable("false")) decoder_1 (
    .out0(if_output), .out1(if_input), .out2(Rwd), .out3(DMwe), .out4(br1), .out5(br2), .out6(\or ),
    .out7(\and ), .out8(addi), .out9(add), .out10(sub), .out11(shra), .out12(shl), .out13(j), .out14(JAL),
    .out15(JR), .sel(opcode));
  or or_4 (or_4_out, addi, Rwd);
  not not_1 (Rdst, or_4_out);
  or or_5 (ALUinB, addi, DMwe, Rwd);
  or or_6 (RWE, add, \or , \and , addi, JAL, sub, shra, shl, Rwd, if_input);
  or or_7 (JP, j, JAL);

  // Other names for the same wires on the sheet: beq = br1; bgt = br2; input = if_input; lw = Rwd; output = if_output;
  //   sw = DMwe
endmodule

module memory_latch (
  input  [15:0] address,
  input  WE,
  input  clk,
  input  [15:0] data_in,
  output [15:0] address_latched,
  output WE_latched,
  output OE_latched,
  output [15:0] data_in_latched
);

  wire d_ff_1_q;
  wire [15:0] register_1_q;

  Register #(.width(16), .trigger("falling")) register_1 (
    .D(address), .en(WE), .clk(clk), .Q(register_1_q));  // open: clr
  D_Flip_Flop #(.trigger("falling")) d_ff_1 (.D(WE), .clk(clk), .Q(d_ff_1_q));  // open: Qn, preset, reset
  Register #(.width(16), .trigger("falling")) register_2 (
    .D(data_in), .en(WE), .clk(clk), .Q(data_in_latched));  // open: clr
  Multiplexer #(.width(16), .enable("false")) multiplexer_1 (
    .in0(address), .in1(register_1_q), .out(address_latched), .sel(d_ff_1_q));
  and and_1 (WE_latched, clk, d_ff_1_q);
  not not_1 (OE_latched, WE_latched);
endmodule

module shra (
  input  [15:0] rs,
  input  [2:0] shamt,
  output [15:0] rd
);

  wire multiplexer_1_out, multiplexer_2_out, multiplexer_3_out, multiplexer_4_out, multiplexer_5_out,
       multiplexer_6_out, multiplexer_7_out, multiplexer_8_out, multiplexer_9_out, multiplexer_10_out,
       multiplexer_11_out, multiplexer_12_out, multiplexer_13_out, multiplexer_14_out, multiplexer_15_out,
       multiplexer_16_out, multiplexer_17_out, multiplexer_18_out, multiplexer_19_out, multiplexer_20_out,
       multiplexer_21_out, multiplexer_22_out, multiplexer_23_out, multiplexer_24_out, multiplexer_25_out,
       multiplexer_26_out, multiplexer_27_out, multiplexer_28_out, multiplexer_29_out, multiplexer_30_out,
       multiplexer_31_out, multiplexer_32_out;

  Multiplexer #(.enable("false")) multiplexer_1 (.in0(rs[0]), .in1(rs[1]), .out(multiplexer_1_out), .sel(shamt[0]));
  Multiplexer #(.enable("false")) multiplexer_2 (.in0(rs[1]), .in1(rs[2]), .out(multiplexer_2_out), .sel(shamt[0]));
  Multiplexer #(.enable("false")) multiplexer_3 (.in0(rs[2]), .in1(rs[3]), .out(multiplexer_3_out), .sel(shamt[0]));
  Multiplexer #(.enable("false")) multiplexer_4 (.in0(rs[3]), .in1(rs[4]), .out(multiplexer_4_out), .sel(shamt[0]));
  Multiplexer #(.enable("false")) multiplexer_5 (.in0(rs[4]), .in1(rs[5]), .out(multiplexer_5_out), .sel(shamt[0]));
  Multiplexer #(.enable("false")) multiplexer_6 (.in0(rs[5]), .in1(rs[6]), .out(multiplexer_6_out), .sel(shamt[0]));
  Multiplexer #(.enable("false")) multiplexer_7 (.in0(rs[6]), .in1(rs[7]), .out(multiplexer_7_out), .sel(shamt[0]));
  Multiplexer #(.enable("false")) multiplexer_8 (.in0(rs[7]), .in1(rs[8]), .out(multiplexer_8_out), .sel(shamt[0]));
  Multiplexer #(.enable("false")) multiplexer_9 (.in0(rs[8]), .in1(rs[9]), .out(multiplexer_9_out), .sel(shamt[0]));
  Multiplexer #(.enable("false")) multiplexer_10 (.in0(rs[9]), .in1(rs[10]), .out(multiplexer_10_out), .sel(shamt[0]));
  Multiplexer #(.enable("false")) multiplexer_11 (.in0(rs[10]), .in1(rs[11]), .out(multiplexer_11_out), .sel(shamt[0]));
  Multiplexer #(.enable("false")) multiplexer_12 (.in0(rs[11]), .in1(rs[12]), .out(multiplexer_12_out), .sel(shamt[0]));
  Multiplexer #(.enable("false")) multiplexer_13 (.in0(rs[12]), .in1(rs[13]), .out(multiplexer_13_out), .sel(shamt[0]));
  Multiplexer #(.enable("false")) multiplexer_14 (.in0(rs[13]), .in1(rs[14]), .out(multiplexer_14_out), .sel(shamt[0]));
  Multiplexer #(.enable("false")) multiplexer_15 (.in0(rs[14]), .in1(rs[15]), .out(multiplexer_15_out), .sel(shamt[0]));
  Multiplexer #(.enable("false")) multiplexer_16 (.in0(rs[15]), .in1(rs[15]), .out(multiplexer_16_out), .sel(shamt[0]));
  Multiplexer #(.enable("false")) multiplexer_17 (
    .in0(multiplexer_1_out), .in1(multiplexer_3_out), .out(multiplexer_17_out), .sel(shamt[1]));
  Multiplexer #(.enable("false")) multiplexer_18 (
    .in0(multiplexer_2_out), .in1(multiplexer_4_out), .out(multiplexer_18_out), .sel(shamt[1]));
  Multiplexer #(.enable("false")) multiplexer_19 (
    .in0(multiplexer_3_out), .in1(multiplexer_5_out), .out(multiplexer_19_out), .sel(shamt[1]));
  Multiplexer #(.enable("false")) multiplexer_20 (
    .in0(multiplexer_4_out), .in1(multiplexer_6_out), .out(multiplexer_20_out), .sel(shamt[1]));
  Multiplexer #(.enable("false")) multiplexer_21 (
    .in0(multiplexer_5_out), .in1(multiplexer_7_out), .out(multiplexer_21_out), .sel(shamt[1]));
  Multiplexer #(.enable("false")) multiplexer_22 (
    .in0(multiplexer_6_out), .in1(multiplexer_8_out), .out(multiplexer_22_out), .sel(shamt[1]));
  Multiplexer #(.enable("false")) multiplexer_23 (
    .in0(multiplexer_7_out), .in1(multiplexer_9_out), .out(multiplexer_23_out), .sel(shamt[1]));
  Multiplexer #(.enable("false")) multiplexer_24 (
    .in0(multiplexer_8_out), .in1(multiplexer_10_out), .out(multiplexer_24_out), .sel(shamt[1]));
  Multiplexer #(.enable("false")) multiplexer_25 (
    .in0(multiplexer_9_out), .in1(multiplexer_11_out), .out(multiplexer_25_out), .sel(shamt[1]));
  Multiplexer #(.enable("false")) multiplexer_26 (
    .in0(multiplexer_10_out), .in1(multiplexer_12_out), .out(multiplexer_26_out), .sel(shamt[1]));
  Multiplexer #(.enable("false")) multiplexer_27 (
    .in0(multiplexer_11_out), .in1(multiplexer_13_out), .out(multiplexer_27_out), .sel(shamt[1]));
  Multiplexer #(.enable("false")) multiplexer_28 (
    .in0(multiplexer_12_out), .in1(multiplexer_14_out), .out(multiplexer_28_out), .sel(shamt[1]));
  Multiplexer #(.enable("false")) multiplexer_29 (
    .in0(multiplexer_13_out), .in1(multiplexer_15_out), .out(multiplexer_29_out), .sel(shamt[1]));
  Multiplexer #(.enable("false")) multiplexer_30 (
    .in0(multiplexer_14_out), .in1(multiplexer_16_out), .out(multiplexer_30_out), .sel(shamt[1]));
  Multiplexer #(.enable("false")) multiplexer_31 (
    .in0(multiplexer_15_out), .in1(rs[15]), .out(multiplexer_31_out), .sel(shamt[1]));
  Multiplexer #(.enable("false")) multiplexer_32 (
    .in0(multiplexer_16_out), .in1(rs[15]), .out(multiplexer_32_out), .sel(shamt[1]));
  Multiplexer #(.enable("false")) multiplexer_33 (
    .in0(multiplexer_17_out), .in1(multiplexer_21_out), .out(rd[0]), .sel(shamt[2]));
  Multiplexer #(.enable("false")) multiplexer_34 (
    .in0(multiplexer_18_out), .in1(multiplexer_22_out), .out(rd[1]), .sel(shamt[2]));
  Multiplexer #(.enable("false")) multiplexer_35 (
    .in0(multiplexer_19_out), .in1(multiplexer_23_out), .out(rd[2]), .sel(shamt[2]));
  Multiplexer #(.enable("false")) multiplexer_36 (
    .in0(multiplexer_20_out), .in1(multiplexer_24_out), .out(rd[3]), .sel(shamt[2]));
  Multiplexer #(.enable("false")) multiplexer_37 (
    .in0(multiplexer_21_out), .in1(multiplexer_25_out), .out(rd[4]), .sel(shamt[2]));
  Multiplexer #(.enable("false")) multiplexer_38 (
    .in0(multiplexer_22_out), .in1(multiplexer_26_out), .out(rd[5]), .sel(shamt[2]));
  Multiplexer #(.enable("false")) multiplexer_39 (
    .in0(multiplexer_23_out), .in1(multiplexer_27_out), .out(rd[6]), .sel(shamt[2]));
  Multiplexer #(.enable("false")) multiplexer_40 (
    .in0(multiplexer_24_out), .in1(multiplexer_28_out), .out(rd[7]), .sel(shamt[2]));
  Multiplexer #(.enable("false")) multiplexer_41 (
    .in0(multiplexer_25_out), .in1(multiplexer_29_out), .out(rd[8]), .sel(shamt[2]));
  Multiplexer #(.enable("false")) multiplexer_42 (
    .in0(multiplexer_26_out), .in1(multiplexer_30_out), .out(rd[9]), .sel(shamt[2]));
  Multiplexer #(.enable("false")) multiplexer_43 (
    .in0(multiplexer_27_out), .in1(multiplexer_31_out), .out(rd[10]), .sel(shamt[2]));
  Multiplexer #(.enable("false")) multiplexer_44 (
    .in0(multiplexer_28_out), .in1(multiplexer_32_out), .out(rd[11]), .sel(shamt[2]));
  Multiplexer #(.enable("false")) multiplexer_45 (.in0(multiplexer_29_out), .in1(rs[15]), .out(rd[12]), .sel(shamt[2]));
  Multiplexer #(.enable("false")) multiplexer_46 (.in0(multiplexer_30_out), .in1(rs[15]), .out(rd[13]), .sel(shamt[2]));
  Multiplexer #(.enable("false")) multiplexer_47 (.in0(multiplexer_31_out), .in1(rs[15]), .out(rd[14]), .sel(shamt[2]));
  Multiplexer #(.enable("false")) multiplexer_48 (.in0(multiplexer_32_out), .in1(rs[15]), .out(rd[15]), .sel(shamt[2]));

  // Other names for the same wires on the sheet: out0 = rd[0]; out1 = rd[1]; out2 = rd[2]; out3 = rd[3]; out4 = rd[4];
  //   out5 = rd[5]; out6 = rd[6]; out7 = rd[7]; out8 = rd[8]; out9 = rd[9]; out10 = rd[10]; out11 = rd[11];
  //   out12 = rd[12]; out13 = rd[13]; out14 = rd[14]; out15 = rd[15]; in0 = rs[0]; in1 = rs[1]; in2 = rs[2];
  //   in3 = rs[3]; in4 = rs[4]; in5 = rs[5]; in6 = rs[6]; in7 = rs[7]; in8 = rs[8]; in9 = rs[9]; in10 = rs[10];
  //   in11 = rs[11]; in12 = rs[12]; in13 = rs[13]; in14 = rs[14]; in15 = rs[15]
endmodule

module shl (
  input  [15:0] rs,
  input  [2:0] shamt,
  output [15:0] rd
);

  wire multiplexer_1_out, multiplexer_2_out, multiplexer_3_out, multiplexer_4_out, multiplexer_5_out,
       multiplexer_6_out, multiplexer_7_out, multiplexer_8_out, multiplexer_9_out, multiplexer_10_out,
       multiplexer_11_out, multiplexer_12_out, multiplexer_13_out, multiplexer_14_out, multiplexer_15_out,
       multiplexer_16_out, multiplexer_17_out, multiplexer_18_out, multiplexer_19_out, multiplexer_20_out,
       multiplexer_21_out, multiplexer_22_out, multiplexer_23_out, multiplexer_24_out, multiplexer_25_out,
       multiplexer_26_out, multiplexer_27_out, multiplexer_28_out, multiplexer_29_out, multiplexer_30_out,
       multiplexer_31_out, multiplexer_32_out;

  Multiplexer #(.enable("false")) multiplexer_1 (.in0(rs[15]), .in1(rs[14]), .out(multiplexer_1_out), .sel(shamt[0]));
  Multiplexer #(.enable("false")) multiplexer_2 (.in0(rs[14]), .in1(rs[13]), .out(multiplexer_2_out), .sel(shamt[0]));
  Multiplexer #(.enable("false")) multiplexer_3 (.in0(rs[13]), .in1(rs[12]), .out(multiplexer_3_out), .sel(shamt[0]));
  Multiplexer #(.enable("false")) multiplexer_4 (.in0(rs[12]), .in1(rs[11]), .out(multiplexer_4_out), .sel(shamt[0]));
  Multiplexer #(.enable("false")) multiplexer_5 (.in0(rs[11]), .in1(rs[10]), .out(multiplexer_5_out), .sel(shamt[0]));
  Multiplexer #(.enable("false")) multiplexer_6 (.in0(rs[10]), .in1(rs[9]), .out(multiplexer_6_out), .sel(shamt[0]));
  Multiplexer #(.enable("false")) multiplexer_7 (.in0(rs[9]), .in1(rs[8]), .out(multiplexer_7_out), .sel(shamt[0]));
  Multiplexer #(.enable("false")) multiplexer_8 (.in0(rs[8]), .in1(rs[7]), .out(multiplexer_8_out), .sel(shamt[0]));
  Multiplexer #(.enable("false")) multiplexer_9 (.in0(rs[7]), .in1(rs[6]), .out(multiplexer_9_out), .sel(shamt[0]));
  Multiplexer #(.enable("false")) multiplexer_10 (.in0(rs[6]), .in1(rs[5]), .out(multiplexer_10_out), .sel(shamt[0]));
  Multiplexer #(.enable("false")) multiplexer_11 (.in0(rs[5]), .in1(rs[4]), .out(multiplexer_11_out), .sel(shamt[0]));
  Multiplexer #(.enable("false")) multiplexer_12 (.in0(rs[4]), .in1(rs[3]), .out(multiplexer_12_out), .sel(shamt[0]));
  Multiplexer #(.enable("false")) multiplexer_13 (.in0(rs[3]), .in1(rs[2]), .out(multiplexer_13_out), .sel(shamt[0]));
  Multiplexer #(.enable("false")) multiplexer_14 (.in0(rs[2]), .in1(rs[1]), .out(multiplexer_14_out), .sel(shamt[0]));
  Multiplexer #(.enable("false")) multiplexer_15 (.in0(rs[1]), .in1(rs[0]), .out(multiplexer_15_out), .sel(shamt[0]));
  Multiplexer #(.enable("false")) multiplexer_16 (.in0(rs[0]), .in1(1'b0), .out(multiplexer_16_out), .sel(shamt[0]));
  Multiplexer #(.enable("false")) multiplexer_17 (
    .in0(multiplexer_1_out), .in1(multiplexer_3_out), .out(multiplexer_17_out), .sel(shamt[1]));
  Multiplexer #(.enable("false")) multiplexer_18 (
    .in0(multiplexer_2_out), .in1(multiplexer_4_out), .out(multiplexer_18_out), .sel(shamt[1]));
  Multiplexer #(.enable("false")) multiplexer_19 (
    .in0(multiplexer_3_out), .in1(multiplexer_5_out), .out(multiplexer_19_out), .sel(shamt[1]));
  Multiplexer #(.enable("false")) multiplexer_20 (
    .in0(multiplexer_4_out), .in1(multiplexer_6_out), .out(multiplexer_20_out), .sel(shamt[1]));
  Multiplexer #(.enable("false")) multiplexer_21 (
    .in0(multiplexer_5_out), .in1(multiplexer_7_out), .out(multiplexer_21_out), .sel(shamt[1]));
  Multiplexer #(.enable("false")) multiplexer_22 (
    .in0(multiplexer_6_out), .in1(multiplexer_8_out), .out(multiplexer_22_out), .sel(shamt[1]));
  Multiplexer #(.enable("false")) multiplexer_23 (
    .in0(multiplexer_7_out), .in1(multiplexer_9_out), .out(multiplexer_23_out), .sel(shamt[1]));
  Multiplexer #(.enable("false")) multiplexer_24 (
    .in0(multiplexer_8_out), .in1(multiplexer_10_out), .out(multiplexer_24_out), .sel(shamt[1]));
  Multiplexer #(.enable("false")) multiplexer_25 (
    .in0(multiplexer_9_out), .in1(multiplexer_11_out), .out(multiplexer_25_out), .sel(shamt[1]));
  Multiplexer #(.enable("false")) multiplexer_26 (
    .in0(multiplexer_10_out), .in1(multiplexer_12_out), .out(multiplexer_26_out), .sel(shamt[1]));
  Multiplexer #(.enable("false")) multiplexer_27 (
    .in0(multiplexer_11_out), .in1(multiplexer_13_out), .out(multiplexer_27_out), .sel(shamt[1]));
  Multiplexer #(.enable("false")) multiplexer_28 (
    .in0(multiplexer_12_out), .in1(multiplexer_14_out), .out(multiplexer_28_out), .sel(shamt[1]));
  Multiplexer #(.enable("false")) multiplexer_29 (
    .in0(multiplexer_13_out), .in1(multiplexer_15_out), .out(multiplexer_29_out), .sel(shamt[1]));
  Multiplexer #(.enable("false")) multiplexer_30 (
    .in0(multiplexer_14_out), .in1(multiplexer_16_out), .out(multiplexer_30_out), .sel(shamt[1]));
  Multiplexer #(.enable("false")) multiplexer_31 (
    .in0(multiplexer_15_out), .in1(1'b0), .out(multiplexer_31_out), .sel(shamt[1]));
  Multiplexer #(.enable("false")) multiplexer_32 (
    .in0(multiplexer_16_out), .in1(1'b0), .out(multiplexer_32_out), .sel(shamt[1]));
  Multiplexer #(.enable("false")) multiplexer_33 (
    .in0(multiplexer_17_out), .in1(multiplexer_21_out), .out(rd[15]), .sel(shamt[2]));
  Multiplexer #(.enable("false")) multiplexer_34 (
    .in0(multiplexer_18_out), .in1(multiplexer_22_out), .out(rd[14]), .sel(shamt[2]));
  Multiplexer #(.enable("false")) multiplexer_35 (
    .in0(multiplexer_19_out), .in1(multiplexer_23_out), .out(rd[13]), .sel(shamt[2]));
  Multiplexer #(.enable("false")) multiplexer_36 (
    .in0(multiplexer_20_out), .in1(multiplexer_24_out), .out(rd[12]), .sel(shamt[2]));
  Multiplexer #(.enable("false")) multiplexer_37 (
    .in0(multiplexer_21_out), .in1(multiplexer_25_out), .out(rd[11]), .sel(shamt[2]));
  Multiplexer #(.enable("false")) multiplexer_38 (
    .in0(multiplexer_22_out), .in1(multiplexer_26_out), .out(rd[10]), .sel(shamt[2]));
  Multiplexer #(.enable("false")) multiplexer_39 (
    .in0(multiplexer_23_out), .in1(multiplexer_27_out), .out(rd[9]), .sel(shamt[2]));
  Multiplexer #(.enable("false")) multiplexer_40 (
    .in0(multiplexer_24_out), .in1(multiplexer_28_out), .out(rd[8]), .sel(shamt[2]));
  Multiplexer #(.enable("false")) multiplexer_41 (
    .in0(multiplexer_25_out), .in1(multiplexer_29_out), .out(rd[7]), .sel(shamt[2]));
  Multiplexer #(.enable("false")) multiplexer_42 (
    .in0(multiplexer_26_out), .in1(multiplexer_30_out), .out(rd[6]), .sel(shamt[2]));
  Multiplexer #(.enable("false")) multiplexer_43 (
    .in0(multiplexer_27_out), .in1(multiplexer_31_out), .out(rd[5]), .sel(shamt[2]));
  Multiplexer #(.enable("false")) multiplexer_44 (
    .in0(multiplexer_28_out), .in1(multiplexer_32_out), .out(rd[4]), .sel(shamt[2]));
  Multiplexer #(.enable("false")) multiplexer_45 (.in0(multiplexer_29_out), .in1(1'b0), .out(rd[3]), .sel(shamt[2]));
  Multiplexer #(.enable("false")) multiplexer_46 (.in0(multiplexer_30_out), .in1(1'b0), .out(rd[2]), .sel(shamt[2]));
  Multiplexer #(.enable("false")) multiplexer_47 (.in0(multiplexer_31_out), .in1(1'b0), .out(rd[1]), .sel(shamt[2]));
  Multiplexer #(.enable("false")) multiplexer_48 (.in0(multiplexer_32_out), .in1(1'b0), .out(rd[0]), .sel(shamt[2]));

  // Other names for the same wires on the sheet: out0 = rd[0]; out1 = rd[1]; out2 = rd[2]; out3 = rd[3]; out4 = rd[4];
  //   out5 = rd[5]; out6 = rd[6]; out7 = rd[7]; out8 = rd[8]; out9 = rd[9]; out10 = rd[10]; out11 = rd[11];
  //   out12 = rd[12]; out13 = rd[13]; out14 = rd[14]; out15 = rd[15]; in0 = rs[0]; in1 = rs[1]; in2 = rs[2];
  //   in3 = rs[3]; in4 = rs[4]; in5 = rs[5]; in6 = rs[6]; in7 = rs[7]; in8 = rs[8]; in9 = rs[9]; in10 = rs[10];
  //   in11 = rs[11]; in12 = rs[12]; in13 = rs[13]; in14 = rs[14]; in15 = rs[15]
endmodule

module subtrct (
  input  [15:0] B,
  input  [15:0] A,
  output [15:0] data_out
);

  full_adder full_adder_1 (.B(B), .A(A), .result(data_out), .sub(1'b1));  // open: ovf
endmodule

module data_reader (
  input  [6:0] orginal_data,
  input  if_valid,
  output [15:0] data_read
);

  Multiplexer #(.width(16), .enable("false")) multiplexer_1 (
    .in0(16'h80), .in1({{9{1'b0}}, orginal_data}), .out(data_read), .sel(if_valid));

  // Other names for the same wires on the sheet: original[6:0] = orginal_data; read_if_valid[6:0] = orginal_data
endmodule
